// Logisim project alu.circ as structural Verilog: 1 circuit, main circuit alu
module alu (
  input  [31:0] A,
  input  [31:0] B,
  input  [3:0] ALUSel,
  output [31:0] ALUResult
);

  wire comparator_1_lt;
  wire [31:0] add_1, and_1, bsel_1, mul_1, mulh_1, mulhu_1, or_1, sll_1, slt_1, sra_1, srl_1, sub_1, xor_1;

  Multiplexer #(.select(4), .width(32)) multiplexer_1 (
    .in0(add_1), .in1(sll_1), .in2(slt_1), .in4(xor_1), .in5(srl_1), .in6(or_1), .in7(and_1), .in8(mul_1),
    .in9(mulh_1), .in11(mulhu_1), .in12(sub_1), .in13(sra_1), .in15(bsel_1), .out(ALUResult), .sel(ALUSel));  // open: in3, in10, in14
  Multiplier #(.width(32)) multiplier_1 (.a(A), .b(B), .out(mul_1));  // open: cin, cout
  Adder #(.width(32)) adder_1 (.a(A), .b(B), .out(add_1));  // open: cin, cout
  Shifter #(.width(32)) shifter_1 (.in(A), .\dist (B[4:0]), .out(sll_1));
  Comparator #(.width(32)) comparator_1 (.a(A), .b(B), .lt(comparator_1_lt));  // open: gt, eq
  assign xor_1 = A ^ B;  // XOR_Gate xor_1, 32 bits wide
  Shifter #(.shift("lr"), .width(32)) shifter_2 (.in(A), .\dist (B[4:0]), .out(srl_1));
  assign or_1 = A | B;  // OR_Gate or_1, 32 bits wide
  assign and_1 = A & B;  // AND_Gate and_1, 32 bits wide
  assign slt_1 = {{31{1'b0}}, comparator_1_lt};  // Bit_Extender bit_extender_1

  // Notes on the sheet:
  //   INPUTS to your circuit
  //   DON'T CHANGE THE LOCATIONS OF THE INPUTS AND OUTPUTS!
  //   OUTPUT from your circuit
endmodule
